# Fritzing sketch Stepper_IR (saved by Fritzing 0.9.3b)

parts:
  Raspberry_Pi_1 = Raspberry Pi 3 [part_number=RPI-3-V1.2]
  BREAKOUT1 = ULN2003A breakout board
  MOTOR1 = 28BYJ-48 Stepper Motor  # not connected
  Part1 = IR Receiver Breakout [package=PCB]

nets:
  3V3: Raspberry_Pi_1.3v3, Part1.VCC
  N1: Raspberry_Pi_1.GIPO5, BREAKOUT1.In_1
  N2: Raspberry_Pi_1.GIPO6, BREAKOUT1.In_2
  N3: Raspberry_Pi_1.GIPO13, BREAKOUT1.In_3
  N4: Raspberry_Pi_1.GIPO19, BREAKOUT1.In_4
  N5: Raspberry_Pi_1.GIPO18, Part1.OUT
  GND: Raspberry_Pi_1.GND, BREAKOUT1.0V, Part1.GND
  5V: Raspberry_Pi_1.5V, BREAKOUT1.+5V

custom parts:
  ULN2003A breakout board: ULN2003A 7-way Darlington Transistor Driver on breakoutboard
