# Fritzing sketch astroberryIO (saved by Fritzing 0.9.3b)
perfboards: 1

parts:
  J1 = female pin header, 20 pins [form="♀ (female)"]
  J2 = female pin header, 20 pins [form="♀ (female)"]
  OLED1 = OLED 128x64 I2C Monochrome Display VDD-GND
  S1 = Momentary Switch [package=ksa_sealed_tac_switch]
  J3 = male pin header, 4 pins [form="♂ (male)"]
  J4 = male pin header, 6 pins [form="♂ (male)"]
  IR1 = vs1838b [package=THT]
  J5 = male pin header, 2 pins [form="♂ (male)"]

nets:
  N1: J1.pin20, J3.pin1, J4.pin5, J5.pin2
  N2: J2.pin3, J4.pin1
  N3: J2.pin4, J4.pin2
  N4: J2.pin5, J4.pin3
  N5: J2.pin6, J4.pin4
  N6: J2.pin13, IR1.Data
  N7: J2.pin14, J3.pin2
  N8: J2.pin15, J3.pin3
  GND: J2.pin16, OLED1.GND, S1.3, J3.pin4, J4.pin6, IR1.GND, J5.pin1
  N9: J2.pin17, S1.2
  N10: J2.pin18, OLED1.SCK
  N11: J2.pin19, OLED1.SDA
  N12: J2.pin20, OLED1.VDD, IR1.Vs

notes:
  Note: 5v power from 12v-5v converter connect here, but I eventually dropped this and used a power bank

custom parts:
  OLED 128x64 I2C Monochrome Display VDD-GND: OLED 128x64 I2C Monochrome Display. Note: there are two variants of this part, this one is the VDD GND SCK SDA variant. The other is GND VDD SCK SDA. Make sure you select the part that matches your module as using the incorrect part will probably destroy your module! In addition the mounting holes are marked on silkscreen but not by default drilled. If you want drilled mounting holes, copy a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
