# Fritzing sketch astroberryIO_breadboard (saved by Fritzing 0.9.3b)
breadboards: 1

parts:
  Raspberry_Pi_1 = Raspberry Pi 3 [part_number=RPI-3-V1.2]
  OLED1 = OLED 128x64 I2C Monochrome Display VDD-GND
  S2 = Pushbutton [package="[THT]"]
  BREAKOUT2 = ULN2003A breakout board
  MOTOR2 = 28BYJ-48 Stepper Motor  # not connected
  IR1 = vs1838b [package=THT]
  2_Channel_Relay1 = 2 Channel Power Relay

nets:
  3V3: Raspberry_Pi_1.3v3, OLED1.VDD, IR1.Vs
  N1: Raspberry_Pi_1.GPIO2, OLED1.SDA
  N2: Raspberry_Pi_1.GPIO3, OLED1.SCK
  N3: Raspberry_Pi_1.GIPO4, S2.Pin_3, S2.Pin_4
  N4: Raspberry_Pi_1.GIPO17, 2_Channel_Relay1.IN1
  N5: Raspberry_Pi_1.GIPO27, 2_Channel_Relay1.IN2
  N6: Raspberry_Pi_1.GIPO22, IR1.Data
  N7: Raspberry_Pi_1.GIPO5, BREAKOUT2.In_1
  N8: Raspberry_Pi_1.GIPO6, BREAKOUT2.In_2
  N9: Raspberry_Pi_1.GIPO13, BREAKOUT2.In_3
  N10: Raspberry_Pi_1.GIPO19, BREAKOUT2.In_4
  GND: Raspberry_Pi_1.GND, OLED1.GND, S2.Pin_1, S2.Pin_2, BREAKOUT2.0V, IR1.GND, 2_Channel_Relay1.GND
  5V: Raspberry_Pi_1.5V, BREAKOUT2.+5V, 2_Channel_Relay1.VCC

notes:
  5v
  3.3v
  IR Sensor

custom parts:
  OLED 128x64 I2C Monochrome Display VDD-GND: OLED 128x64 I2C Monochrome Display. Note: there are two variants of this part, this one is the VDD GND SCK SDA variant. The other is GND VDD SCK SDA. Make sure you select the part that matches your module as using the incorrect part will probably destroy your module! In addition the mounting holes are marked on silkscreen but not by default drilled. If you want drilled mounting holes, copy a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
  ULN2003A breakout board: ULN2003A 7-way Darlington Transistor Driver on breakoutboard
  2 Channel Power Relay: A 2 channel power relay. The module operates at 5V.
