# Fritzing sketch astroberryIO_breadboard_screenOnly (saved by Fritzing 0.9.3b)
breadboards: 1

parts:
  Raspberry_Pi_1 = Raspberry Pi 3 [part_number=RPI-3-V1.2]
  OLED1 = OLED 128x64 I2C Monochrome Display VDD-GND
  S2 = Pushbutton [package="[THT]"]

nets:
  3V3: Raspberry_Pi_1.3v3, OLED1.VDD
  N1: Raspberry_Pi_1.GPIO2, OLED1.SDA
  N2: Raspberry_Pi_1.GPIO3, OLED1.SCK
  N3: Raspberry_Pi_1.GIPO4, S2.Pin_3, S2.Pin_4
  GND: Raspberry_Pi_1.GND, OLED1.GND, S2.Pin_1, S2.Pin_2

notes:
  5v
  3.3v

custom parts:
  OLED 128x64 I2C Monochrome Display VDD-GND: OLED 128x64 I2C Monochrome Display. Note: there are two variants of this part, this one is the VDD GND SCK SDA variant. The other is GND VDD SCK SDA. Make sure you select the part that matches your module as using the incorrect part will probably destroy your module! In addition the mounting holes are marked on silkscreen but not by default drilled. If you want drilled mounting holes, copy a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
